// Logisim project control-logic.circ as structural Verilog: 1 circuit, main circuit control_logic
module control_logic (
  input  [31:0] Instruction,
  input  BrEq,
  input  BrLt,
  output PCSel,
  output RegWEn,
  output [2:0] ImmSel,
  output BrUn,
  output ASel,
  output BSel,
  output [3:0] ALUSel,
  output MemWEn,
  output [1:0] WBSel
);

  wire and_1_out, comparator_1_gt, demultiplexer_1_out0, demultiplexer_1_out1, demultiplexer_1_out2,
       demultiplexer_1_out3;
  wire [0:0] or_1_out;
  wire [2:0] priority_encoder_1_out;
  wire [5:0] FinalPos, multiplexer_1_out, ROMInput;
  wire [15:14] rom_1_data;

  Demultiplexer #(.enable("false"), .select(3)) demultiplexer_1 (
    .out0(demultiplexer_1_out0), .out1(demultiplexer_1_out1), .out2(demultiplexer_1_out2),
    .out3(demultiplexer_1_out3), .in(1'b1), .sel(Instruction[6:4]));  // open: out4, out5, out6, out7
  Comparator #(.width(6)) comparator_1 (
    .a({3'b000, Instruction[14:12]}), .b(6'b000101), .gt(comparator_1_gt));  // open: eq, lt
  ROM #(.addrWidth(6), .dataWidth(16)) rom_1 (
    .addr(ROMInput), .data({rom_1_data, WBSel, MemWEn, ALUSel, BSel, ASel, BrUn, ImmSel, RegWEn}));
  and and_1 (and_1_out, demultiplexer_1_out1, comparator_1_gt);
  Priority_Encoder priority_encoder_1 (
    .in2(demultiplexer_1_out1), .out(priority_encoder_1_out));  // open: in0, in1, in3, in4, in5, in6, in7, en_in, gs, en_out
  buf or_1 (or_1_out[0], and_1_out);  // OR_Gate
  Multiplexer #(.enable("false"), .select(3), .width(6)) multiplexer_1 (
    .in2(6'b001111), .out(multiplexer_1_out), .sel(priority_encoder_1_out));  // open: in0, in1, in3, in4, in5, in6, in7
  Adder #(.width(6)) adder_1 (
    .a({{5{1'b0}}, or_1_out[0]}), .b({3'b000, Instruction[14:12]}), .out(FinalPos));  // open: cin, cout
  Adder #(.width(6)) adder_2 (.a(multiplexer_1_out), .b(FinalPos), .out(ROMInput));  // open: cin, cout

  // Other names for the same wires on the sheet: Opcode[6:0] = Instruction[6:0]; Position[2:0] = Instruction[14:12]

  // Notes on the sheet:
  //   INPUTS to your circuit
  //   Connect ROM Input here ->
  //   contents of rom_1 (hex, n*v repeats v):
  //   15*0 1043 10c3 1143 1243 12c3 16c3 1343 13c3
  //   ROM FOR CONTROL LOGIC
  //   DON'T CHANGE THE LOCATIONS OF THE INPUTS AND OUTPUTS!
  //   This is only if you choose to do the ROM option
  //   CONNECT
  //   WIRE
  //   TO
  //   USE
  //   ROM
  //   OUTPUT from your circuit
  //   Reminder: If using ROM, use combinational logic for PCSel
endmodule
